// Logisim project Project 1.circ as structural Verilog: 12 circuits, main circuit main
module main (
  input  reset
);

  wire ALUSrc, clk_out, J, Mem2Reg, MemWrite, nPC_sel, RegDst, RegWrite, Zero;
  wire [1:0] alu_1_out_4, controller_1_aluctr_1_0, ExtOp;
  wire [4:0] alu_1_out_4_2, multiplexer_1_out;
  wire [24:0] alu_1_out_4_3;
  wire [31:0] ext_1_out_3, gpr_1_rd1, gpr_1_rd2, ifu_1_instr_31_0, multiplexer_2_out, multiplexer_3_out,
       ram_1_data;

  Clock clk (.out(clk_out));
  IFU ifu_1 (.reset(reset), .clk(clk_out), .nPC_sel(nPC_sel), .Zero(Zero), .Instr_31_0(ifu_1_instr_31_0), .j(J));
  // Probe on ifu_1_instr_31_0
  // Probe on ifu_1_instr_31_0[25:21]
  // Probe on ifu_1_instr_31_0[20:16]
  // Probe on ifu_1_instr_31_0[15:11]
  // Probe on ifu_1_instr_31_0[31:26]
  // Probe on ifu_1_instr_31_0[5:0]
  Controller controller_1 (
    .OpCode(ifu_1_instr_31_0[31:26]), .Funct(ifu_1_instr_31_0[5:0]), .RegDst(RegDst), .ALUSrc(ALUSrc),
    .Mem2Reg(Mem2Reg), .RegWrite(RegWrite), .MemWrite(MemWrite), .nPC_sel(nPC_sel), .j(J),
    .ALUctr_1_0(controller_1_aluctr_1_0), .ExtOp_1_0(ExtOp));
  GPR gpr_1 (
    .clk(clk_out), .WE(RegWrite), .A1(ifu_1_instr_31_0[25:21]), .A3(multiplexer_1_out), .RD1(gpr_1_rd1),
    .RD2(gpr_1_rd2), .reset(reset), .A2(ifu_1_instr_31_0[20:16]), .WD(multiplexer_2_out));
  Multiplexer #(.width(5), .enable("false")) multiplexer_1 (
    .in0(ifu_1_instr_31_0[20:16]), .in1(ifu_1_instr_31_0[15:11]), .out(multiplexer_1_out), .sel(RegDst));
  // Probe on ifu_1_instr_31_0[15:0]
  EXT ext_1 (.in_1(ifu_1_instr_31_0[15:0]), .out_3(ext_1_out_3), .ExtOp(ExtOp));
  Multiplexer #(.width(32), .enable("false")) multiplexer_2 (
    .in0({alu_1_out_4_3, alu_1_out_4_2, alu_1_out_4}), .in1(ram_1_data), .out(multiplexer_2_out),
    .sel(Mem2Reg));
  // Probe on gpr_1_rd1
  Multiplexer #(.width(32), .enable("false")) multiplexer_3 (
    .in0(gpr_1_rd2), .in1(ext_1_out_3), .out(multiplexer_3_out), .sel(ALUSrc));
  ALU alu_1 (
    .out_4({alu_1_out_4_3, alu_1_out_4_2, alu_1_out_4}), .in_3(controller_1_aluctr_1_0), .out_5(Zero),
    .A(gpr_1_rd1), .B(multiplexer_3_out));
  // Probe on multiplexer_3_out
  RAM #(.addrWidth(5), .dataWidth(32), .bus("separate")) ram_1 (
    .addr(alu_1_out_4_2), .din(gpr_1_rd2), .data(ram_1_data), .str(MemWrite), .clk(clk_out));  // open: sel, ld, clr

  // Notes on the sheet:
  //   rs
  //   rt
  //   rd
endmodule

module GPR (
  input  reset,
  input  clk,
  input  [31:0] WD,
  input  [4:0] A1,
  input  WE,
  input  [4:0] A3,
  input  [4:0] A2,
  output [31:0] RD1,
  output [31:0] RD2
);

  wire demultiplexer_1_out0, demultiplexer_1_out1, demultiplexer_1_out2, demultiplexer_1_out3,
       demultiplexer_1_out4, demultiplexer_1_out5, demultiplexer_1_out6, demultiplexer_1_out7,
       demultiplexer_1_out8, demultiplexer_1_out9, demultiplexer_1_out10, demultiplexer_1_out11,
       demultiplexer_1_out12, demultiplexer_1_out13, demultiplexer_1_out14, demultiplexer_1_out15,
       demultiplexer_1_out16, demultiplexer_1_out17, demultiplexer_1_out18, demultiplexer_1_out19,
       demultiplexer_1_out20, demultiplexer_1_out21, demultiplexer_1_out22, demultiplexer_1_out23,
       demultiplexer_1_out24, demultiplexer_1_out25, demultiplexer_1_out26, demultiplexer_1_out27,
       demultiplexer_1_out28, demultiplexer_1_out29, demultiplexer_1_out30, demultiplexer_1_out31;
  wire [31:0] _0, _1, _2, _3, _4, _5, _6, _7, _8, _9, _10, _11, _12, _13, _14, _15, _16, _17, _18, _19, _20,
       _21, _22, _23, _24, _25, _26, _27, _28, _29, _30, _31;

  Demultiplexer #(.select(5), .enable("false")) demultiplexer_1 (
    .out0(demultiplexer_1_out0), .out1(demultiplexer_1_out1), .out2(demultiplexer_1_out2),
    .out3(demultiplexer_1_out3), .out4(demultiplexer_1_out4), .out5(demultiplexer_1_out5),
    .out6(demultiplexer_1_out6), .out7(demultiplexer_1_out7), .out8(demultiplexer_1_out8),
    .out9(demultiplexer_1_out9), .out10(demultiplexer_1_out10), .out11(demultiplexer_1_out11),
    .out12(demultiplexer_1_out12), .out13(demultiplexer_1_out13), .out14(demultiplexer_1_out14),
    .out15(demultiplexer_1_out15), .out16(demultiplexer_1_out16), .out17(demultiplexer_1_out17),
    .out18(demultiplexer_1_out18), .out19(demultiplexer_1_out19), .out20(demultiplexer_1_out20),
    .out21(demultiplexer_1_out21), .out22(demultiplexer_1_out22), .out23(demultiplexer_1_out23),
    .out24(demultiplexer_1_out24), .out25(demultiplexer_1_out25), .out26(demultiplexer_1_out26),
    .out27(demultiplexer_1_out27), .out28(demultiplexer_1_out28), .out29(demultiplexer_1_out29),
    .out30(demultiplexer_1_out30), .out31(demultiplexer_1_out31), .in(WE), .sel(A3));
  Register #(.width(32)) register_1 (.en(demultiplexer_1_out0), .Q(_0), .clk(clk), .clr(reset));  // open: D
  Register #(.width(32)) register_2 (.D(WD), .en(demultiplexer_1_out1), .Q(_1), .clk(clk), .clr(reset));
  Register #(.width(32)) register_3 (.D(WD), .en(demultiplexer_1_out2), .Q(_2), .clk(clk), .clr(reset));
  Register #(.width(32)) register_4 (.D(WD), .en(demultiplexer_1_out3), .Q(_3), .clk(clk), .clr(reset));
  Register #(.width(32)) register_5 (.D(WD), .en(demultiplexer_1_out4), .Q(_4), .clk(clk), .clr(reset));
  Register #(.width(32)) register_6 (.D(WD), .en(demultiplexer_1_out5), .Q(_5), .clk(clk), .clr(reset));
  Register #(.width(32)) register_7 (.D(WD), .en(demultiplexer_1_out6), .Q(_6), .clk(clk), .clr(reset));
  Register #(.width(32)) register_8 (.D(WD), .en(demultiplexer_1_out7), .Q(_7), .clk(clk), .clr(reset));
  Register #(.width(32)) register_9 (.D(WD), .en(demultiplexer_1_out8), .Q(_8), .clk(clk), .clr(reset));
  Register #(.width(32)) register_10 (.D(WD), .en(demultiplexer_1_out9), .Q(_9), .clk(clk), .clr(reset));
  Register #(.width(32)) register_11 (.D(WD), .en(demultiplexer_1_out10), .Q(_10), .clk(clk), .clr(reset));
  Register #(.width(32)) register_12 (.D(WD), .en(demultiplexer_1_out11), .Q(_11), .clk(clk), .clr(reset));
  Register #(.width(32)) register_13 (.D(WD), .en(demultiplexer_1_out12), .Q(_12), .clk(clk), .clr(reset));
  Register #(.width(32)) register_14 (.D(WD), .en(demultiplexer_1_out13), .Q(_13), .clk(clk), .clr(reset));
  Register #(.width(32)) register_15 (.D(WD), .en(demultiplexer_1_out14), .Q(_14), .clk(clk), .clr(reset));
  Register #(.width(32)) register_16 (.D(WD), .en(demultiplexer_1_out15), .Q(_15), .clk(clk), .clr(reset));
  Register #(.width(32)) register_17 (.D(WD), .en(demultiplexer_1_out16), .Q(_16), .clk(clk), .clr(reset));
  Register #(.width(32)) register_18 (.D(WD), .en(demultiplexer_1_out17), .Q(_17), .clk(clk), .clr(reset));
  Register #(.width(32)) register_19 (.D(WD), .en(demultiplexer_1_out18), .Q(_18), .clk(clk), .clr(reset));
  Register #(.width(32)) register_20 (.D(WD), .en(demultiplexer_1_out19), .Q(_19), .clk(clk), .clr(reset));
  Register #(.width(32)) register_21 (.D(WD), .en(demultiplexer_1_out20), .Q(_20), .clk(clk), .clr(reset));
  Register #(.width(32)) register_22 (.D(WD), .en(demultiplexer_1_out21), .Q(_21), .clk(clk), .clr(reset));
  Register #(.width(32)) register_23 (.D(WD), .en(demultiplexer_1_out22), .Q(_22), .clk(clk), .clr(reset));
  Register #(.width(32)) register_24 (.D(WD), .en(demultiplexer_1_out23), .Q(_23), .clk(clk), .clr(reset));
  Register #(.width(32)) register_25 (.D(WD), .en(demultiplexer_1_out24), .Q(_24), .clk(clk), .clr(reset));
  Register #(.width(32)) register_26 (.D(WD), .en(demultiplexer_1_out25), .Q(_25), .clk(clk), .clr(reset));
  Register #(.width(32)) register_27 (.D(WD), .en(demultiplexer_1_out26), .Q(_26), .clk(clk), .clr(reset));
  Register #(.width(32)) register_28 (.D(WD), .en(demultiplexer_1_out27), .Q(_27), .clk(clk), .clr(reset));
  Register #(.width(32)) register_29 (.D(WD), .en(demultiplexer_1_out28), .Q(_28), .clk(clk), .clr(reset));
  Register #(.width(32)) register_30 (.D(WD), .en(demultiplexer_1_out29), .Q(_29), .clk(clk), .clr(reset));
  Register #(.width(32)) register_31 (.D(WD), .en(demultiplexer_1_out30), .Q(_30), .clk(clk), .clr(reset));
  Register #(.width(32)) register_32 (.D(WD), .en(demultiplexer_1_out31), .Q(_31), .clk(clk), .clr(reset));
  Multiplexer #(.select(5), .width(32), .enable("false")) multiplexer_1 (
    .in0(_0), .in1(_1), .in2(_2), .in3(_3), .in4(_4), .in5(_5), .in6(_6), .in7(_7), .in8(_8), .in9(_9),
    .in10(_10), .in11(_11), .in12(_12), .in13(_13), .in14(_14), .in15(_15), .in16(_16), .in17(_17),
    .in18(_18), .in19(_19), .in20(_20), .in21(_21), .in22(_22), .in23(_23), .in24(_24), .in25(_25),
    .in26(_26), .in27(_27), .in28(_28), .in29(_29), .in30(_30), .in31(_31), .out(RD1), .sel(A1));
  Multiplexer #(.select(5), .width(32), .enable("false")) multiplexer_2 (
    .in0(_0), .in1(_1), .in2(_2), .in3(_3), .in4(_4), .in5(_5), .in6(_6), .in7(_7), .in8(_8), .in9(_9),
    .in10(_10), .in11(_11), .in12(_12), .in13(_13), .in14(_14), .in15(_15), .in16(_16), .in17(_17),
    .in18(_18), .in19(_19), .in20(_20), .in21(_21), .in22(_22), .in23(_23), .in24(_24), .in25(_25),
    .in26(_26), .in27(_27), .in28(_28), .in29(_29), .in30(_30), .in31(_31), .out(RD2), .sel(A2));
endmodule

module ALU (
  input  [31:0] A,
  input  [31:0] B,
  input  [1:0] in_3,
  output [31:0] out_4,
  output out_5
);

  wire [31:0] adder_32bit_1_s, or_1_out, sub_32bit_1_s;

  Adder_32bit adder_32bit_1 (.A(A), .B(B), .S(adder_32bit_1_s));
  Sub_32bit sub_32bit_1 (.A(B), .B(A), .S(sub_32bit_1_s));
  assign or_1_out = A | B;  // OR_Gate or_1, 32 bits wide
  Multiplexer #(.select(2), .width(32), .disabled(0), .enable("false")) multiplexer_1 (
    .in0(adder_32bit_1_s), .in1(sub_32bit_1_s), .in2(or_1_out), .out(out_4), .sel(in_3));  // open: in3
  Comparator #(.width(32)) comparator_1 (.a(out_4), .b({32{1'b0}}), .eq(out_5));  // open: gt, lt
endmodule

module IFU (
  input  clk,
  input  reset,
  input  j,
  input  nPC_sel,
  input  Zero,
  output [31:0] Instr_31_0
);

  wire and_1_out;
  wire [29:0] adder_1_out, adder_2_out, bit_extender_1_out, multiplexer_1_out, nPC, register_1_q;

  Register #(.width(30)) register_1 (.D(nPC), .Q(register_1_q), .clk(clk), .clr(reset));  // open: en
  and and_1 (and_1_out, nPC_sel, Zero);
  Adder #(.width(30)) adder_1 (.a(register_1_q), .b(30'h1), .out(adder_1_out));  // open: cin, cout
  assign bit_extender_1_out = {{14{1'b0}}, Instr_31_0[15:0]};  // Bit_Extender bit_extender_1
  Adder #(.width(30)) adder_2 (.a(adder_1_out), .b(bit_extender_1_out), .out(adder_2_out));  // open: cin, cout
  Multiplexer #(.width(30), .enable("false")) multiplexer_1 (
    .in0(adder_1_out), .in1(adder_2_out), .out(multiplexer_1_out), .sel(and_1_out));
  ROM #(.addrWidth(5), .dataWidth(32)) rom_1 (.addr(register_1_q[4:0]), .data(Instr_31_0));  // open: sel
  Multiplexer #(.width(30), .enable("false")) multiplexer_2 (
    .in0(multiplexer_1_out), .in1({adder_1_out[29:26], Instr_31_0[25:0]}), .out(nPC), .sel(j));

  // Other names for the same wires on the sheet: imm16[15:0] = Instr_31_0[15:0]

  // Notes on the sheet:
  //   contents of rom_1 (hex, n*v repeats v):
  //   34030093 340600ae 664021 664823 12a0021 ac090010 8c0a0010 112a0002 3c0bcdcd 8000c0d 340befef
  //   3c094567 8000c07
endmodule

module Controller (
  input  [5:0] OpCode,
  input  [5:0] Funct,
  output RegDst,
  output ALUSrc,
  output Mem2Reg,
  output RegWrite,
  output MemWrite,
  output nPC_sel,
  output j,
  output [1:0] ALUctr_1_0,
  output [1:0] ExtOp_1_0
);

  wire Add_out, addFUN, addOP, addu, lui, not_1_out, not_2_out, not_3_out, not_4_out, not_5_out, not_6_out,
       not_7_out, not_8_out, not_9_out, not_10_out, not_11_out, not_12_out, not_13_out, not_14_out,
       not_15_out, not_16_out, not_17_out, not_18_out, ori, Sign_out, Sub_2_out, subFUN, subOP, subu;

  not not_1 (not_1_out, OpCode[5]);
  not not_2 (not_2_out, OpCode[4]);
  not not_3 (not_3_out, OpCode[3]);
  not not_4 (not_4_out, OpCode[2]);
  not not_5 (not_5_out, OpCode[0]);
  not not_6 (not_6_out, OpCode[1]);
  and u_addOP (addOP, not_1_out, not_2_out, not_3_out, not_4_out, not_6_out, not_5_out);
  and u_subOP (subOP, not_1_out, not_2_out, not_3_out, not_4_out, not_6_out, not_5_out);
  and u_ori (ori, not_1_out, not_2_out, OpCode[3], OpCode[2], not_6_out, OpCode[0]);
  and lw (Mem2Reg, OpCode[5], not_2_out, not_3_out, not_4_out, OpCode[1], OpCode[0]);
  and sw (MemWrite, OpCode[5], not_2_out, OpCode[3], not_4_out, OpCode[1], OpCode[0]);
  and beq (nPC_sel, not_1_out, not_2_out, not_3_out, OpCode[2], not_6_out, not_5_out);
  and u_lui (lui, not_1_out, not_2_out, OpCode[3], OpCode[2], OpCode[1], OpCode[0]);
  and u_j (j, not_1_out, not_2_out, not_3_out, not_4_out, OpCode[1], not_5_out);
  not not_7 (not_7_out, Funct[5]);
  not not_8 (not_8_out, Funct[4]);
  or u_RegDst (RegDst, addu, subu);
  not not_9 (not_9_out, Funct[2]);
  not not_10 (not_10_out, Funct[3]);
  or u_ALUSrc (ALUSrc, ori, Mem2Reg, MemWrite, lui);
  not not_11 (not_11_out, Funct[0]);
  not not_12 (not_12_out, Funct[1]);
  or u_RegWrite (RegWrite, addu, subu, ori, Mem2Reg, lui);
  and u_addFUN (addFUN, Funct[5], not_8_out, not_10_out, not_9_out, not_12_out, Funct[0]);
  and u_subFUN (subFUN, Funct[5], not_8_out, not_10_out, not_9_out, Funct[1], Funct[0]);
  and L (ALUctr_1_0[0], not_13_out, Sub_2_out, not_14_out);
  and H (ALUctr_1_0[1], not_13_out, not_15_out, ori);
  and u_addu (addu, addOP, addFUN);
  and sub (subu, subOP, subFUN);
  or Add (Add_out, addu, Mem2Reg, MemWrite);
  not not_13 (not_13_out, Add_out);
  or Sub_2 (Sub_2_out, subu, nPC_sel);
  not not_14 (not_14_out, ori);
  not not_15 (not_15_out, Sub_2_out);
  or Sign (Sign_out, Mem2Reg, MemWrite);
  not not_16 (not_16_out, ori);
  not not_17 (not_17_out, lui);
  not not_18 (not_18_out, Sign_out);
  and L_2 (ExtOp_1_0[0], not_16_out, Sign_out, not_17_out);
  and H_2 (ExtOp_1_0[1], not_16_out, not_18_out, lui);

  // Other names for the same wires on the sheet: beq = nPC_sel; lw = Mem2Reg; sw = MemWrite
endmodule

module EXT (
  input  [15:0] in_1,
  input  [1:0] ExtOp,
  output [31:0] out_3
);

  wire [31:0] bit_extender_1_out, bit_extender_2_out;

  assign bit_extender_1_out = {{16{1'b0}}, in_1};  // Bit_Extender bit_extender_1
  assign bit_extender_2_out = {{16{in_1[15]}}, in_1};  // Bit_Extender bit_extender_2
  Multiplexer #(.select(2), .width(32), .disabled(0), .enable("false")) multiplexer_1 (
    .in0(bit_extender_1_out), .in1(bit_extender_2_out), .in2({in_1, {16{1'b0}}}), .out(out_3), .sel(ExtOp));  // open: in3
endmodule

module Adder_1bit (
  input  in_1,
  input  in_2,
  input  in_3,
  output out_4,
  output out_5
);

  wire and_1_out, and_2_out, and_3_out;

  ExactlyOne xor_1 (.out(out_4), .in0(in_1), .in1(in_2), .in2(in_3));
  and and_1 (and_1_out, in_1, in_3);
  and and_2 (and_2_out, in_2, in_3);
  and and_3 (and_3_out, in_1, in_2);
  or or_1 (out_5, and_1_out, and_2_out, and_3_out);
endmodule

module Adder_32bit (
  input  [31:0] A,
  input  [31:0] B,
  output [31:0] S
);

  wire adder_1bit_1_out_5, adder_1bit_2_out_5, adder_1bit_3_out_5, adder_1bit_4_out_5, adder_1bit_5_out_5,
       adder_1bit_6_out_5, adder_1bit_7_out_5, adder_1bit_8_out_5, adder_1bit_9_out_5, adder_1bit_10_out_5,
       adder_1bit_11_out_5, adder_1bit_12_out_5, adder_1bit_13_out_5, adder_1bit_14_out_5,
       adder_1bit_15_out_5, adder_1bit_16_out_5, adder_1bit_17_out_5, adder_1bit_18_out_5,
       adder_1bit_19_out_5, adder_1bit_20_out_5, adder_1bit_21_out_5, adder_1bit_22_out_5,
       adder_1bit_23_out_5, adder_1bit_24_out_5, adder_1bit_25_out_5, adder_1bit_26_out_5,
       adder_1bit_27_out_5, adder_1bit_28_out_5, adder_1bit_29_out_5, adder_1bit_30_out_5, halfadder_1_out_4;

  HalfAdder halfadder_1 (.in_1(B[0]), .in_2(A[0]), .out_3(S[0]), .out_4(halfadder_1_out_4));
  Adder_1bit adder_1bit_1 (
    .in_1(B[8]), .in_2(A[8]), .in_3(adder_1bit_28_out_5), .out_4(S[8]), .out_5(adder_1bit_1_out_5));
  Adder_1bit adder_1bit_2 (
    .in_1(B[16]), .in_2(A[16]), .in_3(adder_1bit_29_out_5), .out_4(S[16]), .out_5(adder_1bit_2_out_5));
  Adder_1bit adder_1bit_3 (
    .in_1(B[24]), .in_2(A[24]), .in_3(adder_1bit_30_out_5), .out_4(S[24]), .out_5(adder_1bit_3_out_5));
  Adder_1bit adder_1bit_4 (
    .in_1(B[1]), .in_2(A[1]), .in_3(halfadder_1_out_4), .out_4(S[1]), .out_5(adder_1bit_4_out_5));
  Adder_1bit adder_1bit_5 (
    .in_1(B[9]), .in_2(A[9]), .in_3(adder_1bit_1_out_5), .out_4(S[9]), .out_5(adder_1bit_5_out_5));
  Adder_1bit adder_1bit_6 (
    .in_1(B[17]), .in_2(A[17]), .in_3(adder_1bit_2_out_5), .out_4(S[17]), .out_5(adder_1bit_6_out_5));
  Adder_1bit adder_1bit_7 (
    .in_1(B[25]), .in_2(A[25]), .in_3(adder_1bit_3_out_5), .out_4(S[25]), .out_5(adder_1bit_7_out_5));
  Adder_1bit adder_1bit_8 (
    .in_1(B[2]), .in_2(A[2]), .in_3(adder_1bit_4_out_5), .out_4(S[2]), .out_5(adder_1bit_8_out_5));
  Adder_1bit adder_1bit_9 (
    .in_1(B[10]), .in_2(A[10]), .in_3(adder_1bit_5_out_5), .out_4(S[10]), .out_5(adder_1bit_9_out_5));
  Adder_1bit adder_1bit_10 (
    .in_1(B[18]), .in_2(A[18]), .in_3(adder_1bit_6_out_5), .out_4(S[18]), .out_5(adder_1bit_10_out_5));
  Adder_1bit adder_1bit_11 (
    .in_1(B[26]), .in_2(A[26]), .in_3(adder_1bit_7_out_5), .out_4(S[26]), .out_5(adder_1bit_11_out_5));
  Adder_1bit adder_1bit_12 (
    .in_1(B[3]), .in_2(A[3]), .in_3(adder_1bit_8_out_5), .out_4(S[3]), .out_5(adder_1bit_12_out_5));
  Adder_1bit adder_1bit_13 (
    .in_1(B[11]), .in_2(A[11]), .in_3(adder_1bit_9_out_5), .out_4(S[11]), .out_5(adder_1bit_13_out_5));
  Adder_1bit adder_1bit_14 (
    .in_1(B[19]), .in_2(A[19]), .in_3(adder_1bit_10_out_5), .out_4(S[19]), .out_5(adder_1bit_14_out_5));
  Adder_1bit adder_1bit_15 (
    .in_1(B[27]), .in_2(A[27]), .in_3(adder_1bit_11_out_5), .out_4(S[27]), .out_5(adder_1bit_15_out_5));
  Adder_1bit adder_1bit_16 (
    .in_1(B[4]), .in_2(A[4]), .in_3(adder_1bit_12_out_5), .out_4(S[4]), .out_5(adder_1bit_16_out_5));
  Adder_1bit adder_1bit_17 (
    .in_1(B[12]), .in_2(A[12]), .in_3(adder_1bit_13_out_5), .out_4(S[12]), .out_5(adder_1bit_17_out_5));
  Adder_1bit adder_1bit_18 (
    .in_1(B[20]), .in_2(A[20]), .in_3(adder_1bit_14_out_5), .out_4(S[20]), .out_5(adder_1bit_18_out_5));
  Adder_1bit adder_1bit_19 (
    .in_1(B[28]), .in_2(A[28]), .in_3(adder_1bit_15_out_5), .out_4(S[28]), .out_5(adder_1bit_19_out_5));
  Adder_1bit adder_1bit_20 (
    .in_1(B[5]), .in_2(A[5]), .in_3(adder_1bit_16_out_5), .out_4(S[5]), .out_5(adder_1bit_20_out_5));
  Adder_1bit adder_1bit_21 (
    .in_1(B[13]), .in_2(A[13]), .in_3(adder_1bit_17_out_5), .out_4(S[13]), .out_5(adder_1bit_21_out_5));
  Adder_1bit adder_1bit_22 (
    .in_1(B[21]), .in_2(A[21]), .in_3(adder_1bit_18_out_5), .out_4(S[21]), .out_5(adder_1bit_22_out_5));
  Adder_1bit adder_1bit_23 (
    .in_1(B[29]), .in_2(A[29]), .in_3(adder_1bit_19_out_5), .out_4(S[29]), .out_5(adder_1bit_23_out_5));
  Adder_1bit adder_1bit_24 (
    .in_1(B[6]), .in_2(A[6]), .in_3(adder_1bit_20_out_5), .out_4(S[6]), .out_5(adder_1bit_24_out_5));
  Adder_1bit adder_1bit_25 (
    .in_1(B[14]), .in_2(A[14]), .in_3(adder_1bit_21_out_5), .out_4(S[14]), .out_5(adder_1bit_25_out_5));
  Adder_1bit adder_1bit_26 (
    .in_1(B[22]), .in_2(A[22]), .in_3(adder_1bit_22_out_5), .out_4(S[22]), .out_5(adder_1bit_26_out_5));
  Adder_1bit adder_1bit_27 (
    .in_1(B[30]), .in_2(A[30]), .in_3(adder_1bit_23_out_5), .out_4(S[30]), .out_5(adder_1bit_27_out_5));
  Adder_1bit adder_1bit_28 (
    .in_1(B[7]), .in_2(A[7]), .in_3(adder_1bit_24_out_5), .out_4(S[7]), .out_5(adder_1bit_28_out_5));
  Adder_1bit adder_1bit_29 (
    .in_1(B[15]), .in_2(A[15]), .in_3(adder_1bit_25_out_5), .out_4(S[15]), .out_5(adder_1bit_29_out_5));
  Adder_1bit adder_1bit_30 (
    .in_1(B[23]), .in_2(A[23]), .in_3(adder_1bit_26_out_5), .out_4(S[23]), .out_5(adder_1bit_30_out_5));
  Adder_1bit adder_1bit_31 (.in_1(B[31]), .in_2(A[31]), .in_3(adder_1bit_27_out_5), .out_4(S[31]));  // open: out_5
endmodule

module Subber_32bit (
  input  [31:0] A,
  input  [31:0] B,
  output [31:0] S
);

  wire [31:0] adder_32bit_1_s, not_1_out;

  assign not_1_out = ~B;  // NOT_Gate not_1, 32 bits wide
  // Probe on not_1_out
  Adder_32bit adder_32bit_1 (.A(32'h1), .B(not_1_out), .S(adder_32bit_1_s));
  Adder_32bit adder_32bit_2 (.A(A), .B(adder_32bit_1_s), .S(S));
  // Probe on adder_32bit_1_s
endmodule

module HalfAdder (
  input  in_1,
  input  in_2,
  output out_3,
  output out_4
);

  xor xor_1 (out_3, in_1, in_2);
  and and_1 (out_4, in_1, in_2);
endmodule

module Sub_32bit (
  input  [31:0] A,
  input  [31:0] B,
  output [31:0] S
);

  wire sub_1bit_1_co, sub_1bit_2_co, sub_1bit_3_co, sub_1bit_4_co, sub_1bit_5_co, sub_1bit_6_co,
       sub_1bit_7_co, sub_1bit_8_co, sub_1bit_9_co, sub_1bit_10_co, sub_1bit_11_co, sub_1bit_12_co,
       sub_1bit_13_co, sub_1bit_14_co, sub_1bit_15_co, sub_1bit_16_co, sub_1bit_17_co, sub_1bit_18_co,
       sub_1bit_19_co, sub_1bit_20_co, sub_1bit_21_co, sub_1bit_22_co, sub_1bit_23_co, sub_1bit_24_co,
       sub_1bit_25_co, sub_1bit_26_co, sub_1bit_27_co, sub_1bit_28_co, sub_1bit_29_co, sub_1bit_30_co,
       sub_1bit_31_co;

  Sub_1bit sub_1bit_1 (.A(B[0]), .B(A[0]), .C(1'b0), .S(S[0]), .CO(sub_1bit_1_co));
  Sub_1bit sub_1bit_2 (.A(B[8]), .B(A[8]), .C(sub_1bit_29_co), .S(S[8]), .CO(sub_1bit_2_co));
  Sub_1bit sub_1bit_3 (.A(B[16]), .B(A[16]), .C(sub_1bit_30_co), .S(S[16]), .CO(sub_1bit_3_co));
  Sub_1bit sub_1bit_4 (.A(B[24]), .B(A[24]), .C(sub_1bit_31_co), .S(S[24]), .CO(sub_1bit_4_co));
  Sub_1bit sub_1bit_5 (.A(B[1]), .B(A[1]), .C(sub_1bit_1_co), .S(S[1]), .CO(sub_1bit_5_co));
  Sub_1bit sub_1bit_6 (.A(B[9]), .B(A[9]), .C(sub_1bit_2_co), .S(S[9]), .CO(sub_1bit_6_co));
  Sub_1bit sub_1bit_7 (.A(B[17]), .B(A[17]), .C(sub_1bit_3_co), .S(S[17]), .CO(sub_1bit_7_co));
  Sub_1bit sub_1bit_8 (.A(B[25]), .B(A[25]), .C(sub_1bit_4_co), .S(S[25]), .CO(sub_1bit_8_co));
  Sub_1bit sub_1bit_9 (.A(B[2]), .B(A[2]), .C(sub_1bit_5_co), .S(S[2]), .CO(sub_1bit_9_co));
  Sub_1bit sub_1bit_10 (.A(B[10]), .B(A[10]), .C(sub_1bit_6_co), .S(S[10]), .CO(sub_1bit_10_co));
  Sub_1bit sub_1bit_11 (.A(B[18]), .B(A[18]), .C(sub_1bit_7_co), .S(S[18]), .CO(sub_1bit_11_co));
  Sub_1bit sub_1bit_12 (.A(B[26]), .B(A[26]), .C(sub_1bit_8_co), .S(S[26]), .CO(sub_1bit_12_co));
  Sub_1bit sub_1bit_13 (.A(B[3]), .B(A[3]), .C(sub_1bit_9_co), .S(S[3]), .CO(sub_1bit_13_co));
  Sub_1bit sub_1bit_14 (.A(B[11]), .B(A[11]), .C(sub_1bit_10_co), .S(S[11]), .CO(sub_1bit_14_co));
  Sub_1bit sub_1bit_15 (.A(B[19]), .B(A[19]), .C(sub_1bit_11_co), .S(S[19]), .CO(sub_1bit_15_co));
  Sub_1bit sub_1bit_16 (.A(B[27]), .B(A[27]), .C(sub_1bit_12_co), .S(S[27]), .CO(sub_1bit_16_co));
  Sub_1bit sub_1bit_17 (.A(B[4]), .B(A[4]), .C(sub_1bit_13_co), .S(S[4]), .CO(sub_1bit_17_co));
  Sub_1bit sub_1bit_18 (.A(B[12]), .B(A[12]), .C(sub_1bit_14_co), .S(S[12]), .CO(sub_1bit_18_co));
  Sub_1bit sub_1bit_19 (.A(B[20]), .B(A[20]), .C(sub_1bit_15_co), .S(S[20]), .CO(sub_1bit_19_co));
  Sub_1bit sub_1bit_20 (.A(B[28]), .B(A[28]), .C(sub_1bit_16_co), .S(S[28]), .CO(sub_1bit_20_co));
  Sub_1bit sub_1bit_21 (.A(B[5]), .B(A[5]), .C(sub_1bit_17_co), .S(S[5]), .CO(sub_1bit_21_co));
  Sub_1bit sub_1bit_22 (.A(B[13]), .B(A[13]), .C(sub_1bit_18_co), .S(S[13]), .CO(sub_1bit_22_co));
  Sub_1bit sub_1bit_23 (.A(B[21]), .B(A[21]), .C(sub_1bit_19_co), .S(S[21]), .CO(sub_1bit_23_co));
  Sub_1bit sub_1bit_24 (.A(B[29]), .B(A[29]), .C(sub_1bit_20_co), .S(S[29]), .CO(sub_1bit_24_co));
  Sub_1bit sub_1bit_25 (.A(B[6]), .B(A[6]), .C(sub_1bit_21_co), .S(S[6]), .CO(sub_1bit_25_co));
  Sub_1bit sub_1bit_26 (.A(B[14]), .B(A[14]), .C(sub_1bit_22_co), .S(S[14]), .CO(sub_1bit_26_co));
  Sub_1bit sub_1bit_27 (.A(B[22]), .B(A[22]), .C(sub_1bit_23_co), .S(S[22]), .CO(sub_1bit_27_co));
  Sub_1bit sub_1bit_28 (.A(B[30]), .B(A[30]), .C(sub_1bit_24_co), .S(S[30]), .CO(sub_1bit_28_co));
  Sub_1bit sub_1bit_29 (.A(B[7]), .B(A[7]), .C(sub_1bit_25_co), .S(S[7]), .CO(sub_1bit_29_co));
  Sub_1bit sub_1bit_30 (.A(B[15]), .B(A[15]), .C(sub_1bit_26_co), .S(S[15]), .CO(sub_1bit_30_co));
  Sub_1bit sub_1bit_31 (.A(B[23]), .B(A[23]), .C(sub_1bit_27_co), .S(S[23]), .CO(sub_1bit_31_co));
  Sub_1bit sub_1bit_32 (.A(B[31]), .B(A[31]), .C(sub_1bit_28_co), .S(S[31]));  // open: CO
endmodule

module Sub_1bit (
  input  A,
  input  B,
  input  C,
  output S,
  output CO
);

  wire and_1_out, and_2_out, and_3_out, and_4_out, and_5_out, and_6_out, and_7_out, not_1_out, not_2_out,
       not_3_out, not_4_out, not_5_out, not_6_out, not_7_out, not_8_out;

  not not_1 (not_1_out, A);
  not not_2 (not_2_out, B);
  not not_3 (not_3_out, A);
  not not_4 (not_4_out, C);
  not not_5 (not_5_out, B);
  not not_6 (not_6_out, C);
  not not_7 (not_7_out, A);
  not not_8 (not_8_out, A);
  and and_1 (and_1_out, not_1_out, not_2_out, C);
  and and_2 (and_2_out, not_3_out, B, not_4_out);
  and and_3 (and_3_out, A, not_5_out, not_6_out);
  and and_4 (and_4_out, A, B, C);
  and and_5 (and_5_out, not_7_out, C);
  and and_6 (and_6_out, not_8_out, B);
  and and_7 (and_7_out, B, C);
  or or_1 (S, and_1_out, and_2_out, and_3_out, and_4_out);
  or or_2 (CO, and_5_out, and_6_out, and_7_out);
endmodule
